# Fritzing sketch skjema (saved by Fritzing 0.9.3b)
breadboards: 1

parts:
  Part1 = Photon
  Part3 = TFT 1.8 inch 160x128 w microSD [part_number=358]
  S1 = Momentary Switch [package=ksa_sealed_tac_switch]
  S2 = Momentary Switch [package=ksa_sealed_tac_switch]
  R1 = Resistor [tolerance=±5% resistance=220 package="0402 [SMD]"]
  R2 = Resistor [tolerance=±5% resistance=220 package="0402 [SMD]"]
  T1 = LM35 Temperature Sensor [package="TO92 [THT]"]
  J1 = Piezo Speaker
  LED1 = smd LED [color="Red (633nm)" package="0603 [SMD]"]
  LED2 = smd LED [color="Green (555nm)" package="0603 [SMD]"]
  LED3 = smd LED [color="Red (633nm)" package="0603 [SMD]"]
  part = Water Level Sensor
  LED4 = smd LED [color="Infrared (940nm)" package="0603 [SMD]"]
  R3 = Resistor [tolerance=±5% resistance=220 package="0402 [SMD]"]

nets:
  N1: Part1.A0, Part3.TFTCS
  N2: Part1.A1, T1.Vout
  N3: Part1.A2, Part3.TFTDC
  N4: Part1.A3, Part3.SCLK
  N5: Part1.A5, Part3.MOSI
  N6: Part1.DAC, LED4.anode
  N7: Part1.WKP, part.SIG
  N8: Part1.RX, J1.pin2
  GND: Part1.GND, Part3.LITE, R1.Pin_0, R2.Pin_0, T1.GND, J1.pin1, LED1.cathode, LED2.cathode, LED3.cathode, R3.Pin_0
  N9: Part1.D0, Part3.CARDCS
  3V3: Part1.D1, Part1.3V3, Part3.MISO, S1.1, S1.2, S2.1, S2.2, R2.Pin_1, T1.+Vs, part.VCC
  N10: Part1.D2, S1.3, S1.4, R1.Pin_1
  N11: Part1.D3, LED1.anode, LED2.anode, LED3.anode
  N12: S2.3, S2.4
  N13: LED4.cathode, R3.Pin_1

notes:
  ->GND, VCC, SCL, SDA, RES, DC, CS, BLK

custom parts:
  TFT 1.8 inch 160x128 w microSD: This lovely little display breakout is the best way to add a small, colorful and bright display to any project. Since the display uses 4-wire SPI to communicate and has its own pixel-addressable frame buffer, it can be used with every kind of microcontroller. Even a very small one with low memory and few pins available! The 1.8" display has 128x160 color pixels.
  Water Level Sensor: A water level sensor. This sensor operates at 3V to 5V. The Sig (signal) pin outputs an analogue signal that is in proportion to the amount of water in contact with the sensor.
